# Fritzing sketch REYES-CALZADO MIDTERM (saved by Fritzing 0.8.7b)
breadboards: 1

parts:
  Part1 = Arduino Mega ADK (Rev3)
  R1 = Resistor [tolerance=±5% resistance=570 package=THT]
  R2 = Resistor [tolerance=±5% resistance=400 package=THT]
  R3 = Resistor [tolerance=±5% resistance=560 package=THT]
  R4 = Resistor [tolerance=±5% resistance=320 package=THT]

nets:
  N1: Part1.A0, R1.Pin_1, R2.Pin_0
  N2: Part1.A1, R2.Pin_1, R3.Pin_0
  N3: Part1.A2, R3.Pin_1, R4.Pin_0
  N4: Part1.5V, R4.Pin_1
  N5: Part1.GND, R1.Pin_0

notes:
  KNOWN RESITOR- 570 OHMS
  RESISTOR 1- 400 OHMS
  RESISTOR 2- 560 OHMS
  RESISTOR 3- 320 OHMS
